// Logisim project DIVISOR BINARIO CIRCUITO.circ as structural Verilog: 3 circuits, main circuit main
module main (
  input  B3,
  input  B2,
  input  B1,
  input  B0,
  input  A3,
  input  A2,
  input  A1,
  input  A0,
  output out_9,
  output out_10,
  output out_11,
  output out_12,
  output out_13,
  output out_14,
  output out_15,
  output out_16
);

  wire celula_divisora_1_lo, celula_divisora_2_d_prime, celula_divisora_2_lo, celula_divisora_3_lo,
       celula_divisora_4_d_prime, celula_divisora_4_lo, celula_divisora_5_d_prime, celula_divisora_5_lo,
       celula_divisora_6_d_prime, celula_divisora_6_lo, celula_divisora_7_d_prime, celula_divisora_7_lo,
       celula_divisora_8_lo, celula_divisora_9_lo, celula_divisora_10_d_prime, celula_divisora_10_lo,
       celula_divisora_11_d_prime, celula_divisora_11_lo, celula_divisora_12_d_prime, celula_divisora_12_lo,
       celula_divisora_13_lo, celula_divisora_14_d_prime, celula_divisora_14_lo, celula_divisora_15_lo,
       celula_divisora_16_lo;

  celula_divisora celula_divisora_1 (
    .Lo(celula_divisora_1_lo), .OS(celula_divisora_1_lo), .Y(B3), .X(1'b0), .Li(celula_divisora_2_lo));  // open: D_prime
  not not_1 (out_14, celula_divisora_3_lo);
  not not_2 (out_13, celula_divisora_1_lo);
  celula_divisora celula_divisora_2 (
    .Lo(celula_divisora_2_lo), .OS(celula_divisora_1_lo), .Y(B2), .X(1'b0),
    .D_prime(celula_divisora_2_d_prime), .Li(celula_divisora_4_lo));
  celula_divisora celula_divisora_3 (
    .Lo(celula_divisora_3_lo), .OS(celula_divisora_3_lo), .Y(B3), .X(celula_divisora_2_d_prime),
    .Li(celula_divisora_6_lo));  // open: D_prime
  not not_3 (out_15, celula_divisora_8_lo);
  celula_divisora celula_divisora_4 (
    .Lo(celula_divisora_4_lo), .OS(celula_divisora_1_lo), .Y(B1), .X(1'b0),
    .D_prime(celula_divisora_4_d_prime), .Li(celula_divisora_10_lo));
  celula_divisora celula_divisora_5 (
    .Lo(celula_divisora_5_lo), .OS(celula_divisora_3_lo), .Y(B1), .X(celula_divisora_10_d_prime),
    .D_prime(celula_divisora_5_d_prime), .Li(celula_divisora_11_lo));
  celula_divisora celula_divisora_6 (
    .Lo(celula_divisora_6_lo), .OS(celula_divisora_3_lo), .Y(B2), .X(celula_divisora_4_d_prime),
    .D_prime(celula_divisora_6_d_prime), .Li(celula_divisora_5_lo));
  celula_divisora celula_divisora_7 (
    .Lo(celula_divisora_7_lo), .OS(celula_divisora_8_lo), .Y(B2), .X(celula_divisora_5_d_prime),
    .D_prime(celula_divisora_7_d_prime), .Li(celula_divisora_12_lo));
  celula_divisora celula_divisora_8 (
    .Lo(celula_divisora_8_lo), .OS(celula_divisora_8_lo), .Y(B3), .X(celula_divisora_6_d_prime),
    .Li(celula_divisora_7_lo));  // open: D_prime
  celula_divisora celula_divisora_9 (
    .Lo(celula_divisora_9_lo), .OS(celula_divisora_9_lo), .Y(B3), .X(celula_divisora_7_d_prime),
    .D_prime(out_9), .Li(celula_divisora_13_lo));
  not not_4 (out_16, celula_divisora_9_lo);
  celula_divisora celula_divisora_10 (
    .Lo(celula_divisora_10_lo), .OS(celula_divisora_1_lo), .Y(B0), .X(A3),
    .D_prime(celula_divisora_10_d_prime), .Li(1'b0));
  celula_divisora celula_divisora_11 (
    .Lo(celula_divisora_11_lo), .OS(celula_divisora_3_lo), .Y(B0), .X(A2),
    .D_prime(celula_divisora_11_d_prime), .Li(1'b0));
  celula_divisora celula_divisora_12 (
    .Lo(celula_divisora_12_lo), .OS(celula_divisora_8_lo), .Y(B1), .X(celula_divisora_11_d_prime),
    .D_prime(celula_divisora_12_d_prime), .Li(celula_divisora_14_lo));
  celula_divisora celula_divisora_13 (
    .Lo(celula_divisora_13_lo), .OS(celula_divisora_9_lo), .Y(B2), .X(celula_divisora_12_d_prime),
    .D_prime(out_10), .Li(celula_divisora_15_lo));
  celula_divisora celula_divisora_14 (
    .Lo(celula_divisora_14_lo), .OS(celula_divisora_8_lo), .Y(B0), .X(A1),
    .D_prime(celula_divisora_14_d_prime), .Li(1'b0));
  celula_divisora celula_divisora_15 (
    .Lo(celula_divisora_15_lo), .OS(celula_divisora_9_lo), .Y(B1), .X(celula_divisora_14_d_prime),
    .D_prime(out_11), .Li(celula_divisora_16_lo));
  celula_divisora celula_divisora_16 (
    .Lo(celula_divisora_16_lo), .OS(celula_divisora_9_lo), .Y(B0), .X(A0), .D_prime(out_12), .Li(1'b0));

  // Notes on the sheet:
  //   0-B3
  //   0-B2
  //   A3-B0
  //   0-B1
endmodule

module subtrator (
  input  B,
  input  A,
  input  L1,
  output Lo,
  output D
);

  wire and_1_out, and_2_out, not_1_out, not_2_out, xor_1_out;

  or or_1 (Lo, and_1_out, and_2_out);
  and and_1 (and_1_out, not_1_out, B);
  and and_2 (and_2_out, not_2_out, L1);
  not not_1 (not_1_out, A);
  not not_2 (not_2_out, xor_1_out);
  xor xor_1 (xor_1_out, B, A);
  xor xor_2 (D, L1, xor_1_out);
endmodule

module celula_divisora (
  input  Y,
  input  X,
  input  Li,
  input  OS,
  output Lo,
  output D_prime
);

  wire and_1_out, and_2_out, not_1_out, subtrator_1_d;

  subtrator subtrator_1 (.Lo(Lo), .B(Y), .A(X), .D(subtrator_1_d), .L1(Li));
  and and_1 (and_1_out, subtrator_1_d, OS);
  not not_1 (not_1_out, OS);
  and and_2 (and_2_out, X, not_1_out);
  or or_1 (D_prime, and_1_out, and_2_out);
endmodule
