// Logisim project DIVISOR CIRCUITO 4 BITS.circ as structural Verilog: 1 circuit, main circuit main
module main (
  input  D7,
  input  D6,
  input  D5,
  input  D4,
  input  D3,
  input  D2,
  input  D1,
  input  D0,
  input  in_9,
  input  in_10,
  input  M0,
  input  DR0,
  input  M1,
  input  DR1,
  input  M2,
  input  DR2,
  input  M3,
  input  DR3,
  output out_19,
  output out_20,
  output out_21,
  output out_22,
  output out_23,
  output out_24,
  output out_25,
  output out_26
);

  wire adder_1_out, adder_2_out, adder_3_out, adder_4_out, and_1_out, and_2_out, and_3_out, and_4_out,
       and_5_out, and_6_out, and_7_out, and_8_out, and_9_out, and_10_out, and_11_out, and_12_out, and_13_out,
       and_14_out, and_15_out, clock_1_out, d_ff_2_q, d_ff_3_q, d_ff_4_q, d_ff_5_q, d_ff_6_q, d_ff_7_q,
       d_ff_8_q, d_ff_9_q, d_ff_10_q, multiplexer_6_out, multiplexer_7_out, multiplexer_8_out,
       multiplexer_9_out, multiplexer_12_out, multiplexer_14_out, not_1_out, or_1_out, or_2_out, or_3_out,
       or_4_out, or_5_out, or_6_out, or_7_out, or_8_out, or_9_out, xnor_1_out, xor_1_out, xor_2_out,
       xor_3_out, xor_4_out, xor_5_out, xor_6_out, xor_7_out, xor_8_out, xor_9_out;

  Clock clock_1 (.out(clock_1_out));
  D_Flip_Flop d_ff_1 (.clk(clock_1_out), .D(1'b1), .Qn(clock_1_out));  // open: Q, preset, en, reset
  and and_1 (and_1_out, clock_1_out, D7);
  or or_1 (or_1_out, adder_4_out, and_1_out);
  and and_2 (and_2_out, d_ff_2_q, in_10);
  xnor xnor_1 (xnor_1_out, DR3, and_2_out);
  and and_3 (and_3_out, clock_1_out, D6);
  D_Flip_Flop d_ff_2 (.clk(clock_1_out), .D(or_1_out), .Q(d_ff_2_q));  // open: Qn, preset, en, reset
  or or_2 (or_2_out, adder_3_out, and_3_out);
  Multiplexer multiplexer_1 (.in0(d_ff_2_q), .in1(d_ff_3_q), .out(out_19), .sel(in_10));  // open: en
  D_Flip_Flop d_ff_3 (.clk(clock_1_out), .D(or_2_out), .Q(d_ff_3_q));  // open: Qn, preset, en, reset
  Multiplexer multiplexer_2 (.in0(d_ff_2_q), .in1(d_ff_4_q), .out(out_20), .sel(in_10));  // open: en
  xor xor_1 (xor_1_out, DR0, xnor_1_out);
  xor xor_2 (xor_2_out, DR1, xnor_1_out);
  xor xor_3 (xor_3_out, DR2, xnor_1_out);
  xor xor_4 (xor_4_out, DR3, xnor_1_out);
  and and_4 (and_4_out, clock_1_out, D5);
  or or_3 (or_3_out, adder_2_out, and_4_out);
  Multiplexer multiplexer_3 (.in0(d_ff_3_q), .in1(d_ff_5_q), .out(out_21), .sel(in_10));  // open: en
  and and_5 (and_5_out, clock_1_out, D4);
  D_Flip_Flop d_ff_4 (.clk(clock_1_out), .D(or_3_out), .Q(d_ff_4_q));  // open: Qn, preset, en, reset
  or or_4 (or_4_out, adder_1_out, and_5_out);
  Multiplexer multiplexer_4 (.in0(d_ff_4_q), .in1(d_ff_6_q), .out(out_22), .sel(in_10));  // open: en
  xor xor_5 (xor_5_out, and_10_out, and_6_out);
  and and_6 (and_6_out, xor_9_out, M0);
  xor xor_6 (xor_6_out, and_10_out, and_7_out);
  and and_7 (and_7_out, xor_9_out, M1);
  xor xor_7 (xor_7_out, and_10_out, and_8_out);
  and and_8 (and_8_out, xor_9_out, M2);
  xor xor_8 (xor_8_out, and_10_out, and_9_out);
  and and_9 (and_9_out, xor_9_out, M3);
  D_Flip_Flop d_ff_5 (.clk(clock_1_out), .D(or_4_out), .Q(d_ff_5_q));  // open: Qn, preset, en, reset
  Multiplexer multiplexer_5 (.in0(d_ff_5_q), .in1(d_ff_7_q), .out(out_23), .sel(in_10));  // open: en
  and and_10 (and_10_out, xor_9_out, out_26);
  Multiplexer multiplexer_6 (.in0(xor_5_out), .in1(xor_1_out), .out(multiplexer_6_out), .sel(in_10));  // open: en
  Multiplexer multiplexer_7 (.in0(xor_6_out), .in1(xor_2_out), .out(multiplexer_7_out), .sel(in_10));  // open: en
  Multiplexer multiplexer_8 (.in0(xor_7_out), .in1(xor_3_out), .out(multiplexer_8_out), .sel(in_10));  // open: en
  Multiplexer multiplexer_9 (.in0(xor_8_out), .in1(xor_4_out), .out(multiplexer_9_out), .sel(in_10));  // open: en
  and and_11 (and_11_out, clock_1_out, D3);
  or or_5 (or_5_out, out_23, and_11_out);
  Multiplexer multiplexer_10 (.in0(d_ff_6_q), .in1(d_ff_8_q), .out(out_24), .sel(in_10));  // open: en
  and and_12 (and_12_out, clock_1_out, D2);
  D_Flip_Flop d_ff_6 (.clk(clock_1_out), .D(or_5_out), .Q(d_ff_6_q));  // open: Qn, preset, en, reset
  or or_6 (or_6_out, out_24, and_12_out);
  Multiplexer multiplexer_11 (.in0(d_ff_7_q), .in1(multiplexer_14_out), .out(out_25), .sel(in_10));  // open: en
  Multiplexer multiplexer_12 (.in0(and_10_out), .in1(xnor_1_out), .out(multiplexer_12_out), .sel(in_10));  // open: en
  Adder #(.width(1)) adder_1 (
    .a(out_22), .b(multiplexer_6_out), .out(adder_1_out), .cin(multiplexer_12_out));  // open: cout
  Adder #(.width(1)) adder_2 (.a(out_21), .b(multiplexer_7_out), .out(adder_2_out));  // open: cin, cout
  Adder #(.width(1)) adder_3 (.a(out_20), .b(multiplexer_8_out), .out(adder_3_out));  // open: cin, cout
  Adder #(.width(1)) adder_4 (.a(out_19), .b(multiplexer_9_out), .out(adder_4_out));  // open: cin, cout
  D_Flip_Flop d_ff_7 (.clk(clock_1_out), .D(or_6_out), .Q(d_ff_7_q));  // open: Qn, preset, en, reset
  xor xor_9 (xor_9_out, out_26, d_ff_10_q);
  and and_13 (and_13_out, clock_1_out, D1);
  or or_7 (or_7_out, out_25, and_13_out);
  Multiplexer multiplexer_13 (.in0(d_ff_8_q), .in1(1'b0), .out(out_26), .sel(in_10));  // open: en
  and and_14 (and_14_out, clock_1_out, D0);
  D_Flip_Flop d_ff_8 (.clk(clock_1_out), .D(or_7_out), .Q(d_ff_8_q));  // open: Qn, preset, en, reset
  or or_8 (or_8_out, out_26, and_14_out);
  D_Flip_Flop d_ff_9 (.clk(clock_1_out), .D(or_8_out), .Q(d_ff_9_q));  // open: Qn, preset, en, reset
  Multiplexer multiplexer_14 (.in0(d_ff_9_q), .in1(not_1_out), .out(multiplexer_14_out), .sel(in_9));  // open: en
  and and_15 (and_15_out, clock_1_out, 1'b0);
  not not_1 (not_1_out, adder_4_out);
  or or_9 (or_9_out, d_ff_9_q, and_15_out);
  D_Flip_Flop d_ff_10 (.clk(clock_1_out), .D(or_9_out), .Q(d_ff_10_q), .en(in_10));  // open: Qn, preset, reset
endmodule
