// Logisim project MULTIPLICADOR CIRCUITO 4 BITS.circ as structural Verilog: 5 circuits, main circuit FULL ADDER 4 BITS
module FULL_ADDER_4_BITS (
  input  A0,
  input  A1,
  input  A2,
  input  A3,
  input  CARRY_IN,
  input  B0,
  input  B1,
  input  B2,
  input  B3,
  output SOMA_0,
  output SOMA_1,
  output SOMA2,
  output SOMA_3,
  output CARRY_OUT
);

  wire full_adder_1_carry_out, full_adder_2_carry_out, full_adder_3_carry_out;

  full_adder full_adder_1 (.A(A0), .B(B0), .CARRY_IN(CARRY_IN), .SOMA(SOMA_0), .CARRY_OUT(full_adder_1_carry_out));
  full_adder full_adder_2 (
    .A(A1), .B(B1), .CARRY_IN(full_adder_1_carry_out), .SOMA(SOMA_1), .CARRY_OUT(full_adder_2_carry_out));
  full_adder full_adder_3 (
    .A(A2), .B(B2), .CARRY_IN(full_adder_2_carry_out), .SOMA(SOMA2), .CARRY_OUT(full_adder_3_carry_out));
  full_adder full_adder_4 (.A(A3), .B(B3), .CARRY_IN(full_adder_3_carry_out), .SOMA(SOMA_3), .CARRY_OUT(CARRY_OUT));
endmodule

module full_adder (
  input  A,
  input  B,
  input  CARRY_IN,
  output SOMA,
  output CARRY_OUT
);

  wire and_1_out, and_2_out, xor_1_out;

  xor xor_1 (xor_1_out, A, B);
  and and_1 (and_1_out, A, B);
  xor xor_2 (SOMA, xor_1_out, CARRY_IN);
  and and_2 (and_2_out, xor_1_out, CARRY_IN);
  or or_1 (CARRY_OUT, and_2_out, and_1_out);
endmodule

module half_adder (
  input  A,
  input  B,
  output SOMA,
  output CARRY_OUT
);

  xor xor_1 (SOMA, A, B);
  and and_1 (CARRY_OUT, A, B);
endmodule

module Multilplicador_4_BITS (
  input  A3,
  input  A2,
  input  A1,
  input  A0,
  input  B0,
  input  in_6,
  input  B1,
  input  B2,
  input  B3,
  input  in_10,
  input  in_11,
  output P7,
  output P6,
  output P5,
  output P4,
  output P3,
  output P2,
  output P1,
  output P0
);

  wire and_1_out, and_2_out, and_3_out, and_4_out, and_5_out, and_6_out, and_7_out, and_8_out, and_9_out,
       and_10_out, and_11_out, and_12_out, and_13_out, and_14_out, and_15_out, full_adder_4_bits_2_carry_out,
       full_adder_4_bits_2_soma2, full_adder_4_bits_2_soma_1, full_adder_4_bits_2_soma_3,
       FULL_ADDER_carry_out, FULL_ADDER_soma2, FULL_ADDER_soma_1, FULL_ADDER_soma_3;

  and and_1 (and_1_out, B3, A3);
  and and_2 (and_2_out, B3, A2);
  and and_3 (and_3_out, B3, A1);
  and and_4 (and_4_out, B2, A3);
  and and_5 (and_5_out, B3, A0);
  and and_6 (and_6_out, B2, A2);
  and and_7 (and_7_out, B2, A1);
  FULL_ADDER_4_BITS full_adder_4_bits_1 (
    .A0(FULL_ADDER_soma_1), .A1(FULL_ADDER_soma2), .A2(FULL_ADDER_soma_3), .A3(FULL_ADDER_carry_out),
    .CARRY_IN(in_11), .B0(and_5_out), .B1(and_3_out), .B2(and_2_out), .B3(and_1_out), .SOMA_0(P3),
    .SOMA_1(P4), .SOMA2(P5), .SOMA_3(P6), .CARRY_OUT(P7));
  and and_8 (and_8_out, B1, A3, A3);
  and and_9 (and_9_out, B2, A0);
  and and_10 (and_10_out, B1, A2);
  and and_11 (and_11_out, B1, A1);
  and and_12 (and_12_out, B1, A0);
  and and_13 (and_13_out, B0, A3);
  and and_14 (and_14_out, B0, A2);
  FULL_ADDER_4_BITS FULL_ADDER (
    .A0(full_adder_4_bits_2_soma_1), .A1(full_adder_4_bits_2_soma2), .A2(full_adder_4_bits_2_soma_3),
    .A3(full_adder_4_bits_2_carry_out), .CARRY_IN(in_10), .B0(and_9_out), .B1(and_7_out), .B2(and_6_out),
    .B3(and_4_out), .SOMA_0(P2), .SOMA_1(FULL_ADDER_soma_1), .SOMA2(FULL_ADDER_soma2),
    .SOMA_3(FULL_ADDER_soma_3), .CARRY_OUT(FULL_ADDER_carry_out));
  and and_15 (and_15_out, B0, A1);
  FULL_ADDER_4_BITS full_adder_4_bits_2 (
    .A0(and_15_out), .A1(and_14_out), .A2(and_13_out), .A3(in_6), .CARRY_IN(in_6), .B0(and_12_out),
    .B1(and_11_out), .B2(and_10_out), .B3(and_8_out), .SOMA_0(P1), .SOMA_1(full_adder_4_bits_2_soma_1),
    .SOMA2(full_adder_4_bits_2_soma2), .SOMA_3(full_adder_4_bits_2_soma_3),
    .CARRY_OUT(full_adder_4_bits_2_carry_out));
  and and_16 (P0, B0, A0);

  // Notes on the sheet:
  //   FULL ADDER
endmodule

module MULTIPLICADOR_2_BITS (
  input  A0,
  input  A1,
  input  B0,
  input  B1,
  output P0,
  output P1,
  output P2,
  output P3
);

  wire and_2_out, and_3_out, and_4_out, half_adder_1_carry_out;

  and and_1 (P0, A0, B0);
  and and_2 (and_2_out, A1, B0);
  and and_3 (and_3_out, A0, B1);
  and and_4 (and_4_out, A1, B1);
  half_adder half_adder_1 (.A(and_2_out), .B(and_3_out), .SOMA(P1), .CARRY_OUT(half_adder_1_carry_out));
  half_adder half_adder_2 (.A(half_adder_1_carry_out), .B(and_4_out), .SOMA(P2), .CARRY_OUT(P3));

  // Notes on the sheet:
  //   HALF ADDER
  //   HALF ADDER
endmodule
